// Digital circuit digital_03_01.dig as structural Verilog
module digital_03_01 (
  input  [3:0] In,
  output A,
  output B,
  output C,
  output D,
  output E,
  output F,
  output G
);

  wire and_1_out, and_2_out, and_3_out, and_4_out, and_5_out, and_6_out, nand_1_out, nor_1_out, nor_2_out,
       nor_3_out, nor_4_out, nor_5_out, not_1_out, not_2_out, not_3_out, not_4_out, or_1_out, or_2_out,
       or_3_out, xnor_1_out, xor_1_out;

  or or_1 (or_1_out, In[3], In[1]);
  xor xor_1 (xor_1_out, In[2], In[1]);
  not not_1 (not_1_out, In[0]);
  and and_1 (and_1_out, or_1_out, not_2_out);
  not not_2 (not_2_out, In[0]);
  or or_2 (or_2_out, In[3], In[2]);
  and and_2 (and_2_out, xor_1_out, In[0]);
  and and_3 (and_3_out, In[1], not_1_out);
  nor nor_1 (nor_1_out, In[2], In[1], In[0]);
  nor nor_2 (nor_2_out, In[3], In[2], In[1], In[0]);
  or or_3 (or_3_out, In[3], In[2]);
  nor nor_3 (nor_3_out, In[1], In[0]);
  nand nand_1 (nand_1_out, or_2_out, In[0]);
  and and_4 (and_4_out, In[2], In[0]);
  nor nor_4 (nor_4_out, In[2], In[1], In[0]);
  xnor xnor_1 (xnor_1_out, In[1], In[0]);
  nor nor_5 (nor_5_out, In[3], In[2]);
  and and_5 (and_5_out, nand_1_out, In[1]);
  and and_6 (and_6_out, In[2], not_3_out);
  not not_3 (not_3_out, In[1]);
  not not_4 (not_4_out, In[1]);
  or or_4 (E, nor_2_out, and_1_out);
  or or_5 (F, or_3_out, nor_3_out);
  or or_6 (A, and_4_out, In[3], In[1], nor_4_out);
  or or_7 (B, In[3], xnor_1_out, nor_5_out);
  or or_8 (C, In[3], In[2], not_4_out, In[0]);
  or or_9 (D, In[3], and_2_out, and_3_out, nor_1_out);
  or or_10 (G, In[3], and_5_out, and_6_out);
  Seven_Seg seven_seg_1 (.a(A), .b(B), .c(C), .d(D), .e(E), .f(F), .g(G), .dp(1'b0));

  // Other names for the same wires on the sheet: _1 = In[0]; _2 = In[1]; _4 = In[2]; _8 = In[3]
endmodule
