// Digital circuit 01_Template.dig as structural Verilog
module _01_Template (
  input  A,
  input  B,
  input  C,
  input  D,
  output [3:0] Z
);

  Seven_Seg_Hex seven_seg_hex_1 (.d(Z), .dp(1'b0));
endmodule
