// Digital circuit diglab_01_01.dig as structural Verilog
module diglab_01_01 (
  input  A,
  input  B,
  input  C,
  input  D,
  output [3:0] Z
);

  Seven_Seg_Hex seven_seg_hex_1 (.d({D, C, B, A}), .dp(1'b0));

  assign Z = {D, C, B, A};
endmodule
