// Digital circuit diglab_02_07.dig as structural Verilog
module diglab_02_07 (
  input  X0,
  input  X1,
  input  Selector,
  output Z
);

  wire and_1_out, and_2_out, not_1_out, not_2_out, not_3_out;

  not not_1 (not_1_out, X0);
  not not_2 (not_2_out, X1);
  not not_3 (not_3_out, Selector);
  and and_1 (and_1_out, not_3_out, X0);
  and and_2 (and_2_out, Selector, X1);
  or or_1 (Z, and_1_out, and_2_out);
endmodule
