// Digital circuit diglab_02_09.dig as structural Verilog
module diglab_02_09 (
  input  S1,
  input  S0,
  input  X0,
  input  X1,
  input  X2,
  input  X3,
  output Z
);

  wire and_1_out, and_2_out, and_3_out, and_4_out, not_1_out, not_2_out;

  not not_1 (not_1_out, S0);
  not not_2 (not_2_out, S1);
  and and_1 (and_1_out, not_1_out, not_2_out, X0);
  and and_2 (and_2_out, not_2_out, S0, X1);
  and and_3 (and_3_out, S1, not_1_out, X2);
  and and_4 (and_4_out, S0, S1, X3);
  or or_1 (Z, and_1_out, and_2_out, and_3_out, and_4_out);
endmodule
