// Digital circuit digital_03_02.dig as structural Verilog
module digital_03_02 (
  input  [2:0] In,
  input  clk,
  output [7:0] Z
);

  wire and_1_out, and_2_out, and_3_out, and_4_out, nand_1_out, nor_1_out, nor_2_out, not_1_out, not_2_out,
       or_1_out, or_2_out, or_3_out, xnor_1_out, xor_1_out, xor_2_out;

  xor xor_1 (xor_1_out, In[1], In[0]);
  nand nand_1 (nand_1_out, In[2], In[0]);
  nor nor_1 (nor_1_out, In[2], In[0]);
  xnor xnor_1 (xnor_1_out, In[1], In[0]);
  or or_1 (or_1_out, In[2], xor_1_out);
  or or_2 (or_2_out, In[1], nand_1_out);
  and and_1 (and_1_out, not_1_out, In[0]);
  not not_1 (not_1_out, In[2]);
  and and_2 (and_2_out, In[2], not_2_out);
  not not_2 (not_2_out, In[1]);
  nor nor_2 (nor_2_out, In[2], In[0]);
  xor xor_2 (xor_2_out, In[2], In[1]);
  and and_3 (and_3_out, nor_1_out, In[1]);
  and and_4 (and_4_out, In[2], xnor_1_out);
  or or_3 (or_3_out, In[2], In[1]);
  and and_5 (Z[5], or_1_out, or_2_out);
  or or_4 (Z[3], and_1_out, and_2_out);
  or or_5 (Z[2], nor_2_out, xor_2_out);
  or or_6 (Z[1], and_3_out, and_4_out);
  xor xor_3 (Z[0], In[0], or_3_out);
  Terminal terminal_1 (.D({2'b01, Z[5], 1'b0, Z[3:0]}), .C(clk), .en(1'b1));

  assign {Z[7:6], Z[4]} = 3'b010;

  // Other names for the same wires on the sheet: _1 = Z[0]; _2 = Z[1]; _4 = Z[2]; _8 = Z[3]; _32 = Z[5]; C = In[0];
  //   B = In[1]; A = In[2]
endmodule
