// Digital circuit digital_03_03.dig as structural Verilog
module digital_03_03 (
  input  [3:0] In,
  input  [1:0] Selector,
  output [3:0] Output
);

  wire and_1_out, and_2_out, and_3_out, and_4_out, and_5_out, and_6_out, and_7_out, and_8_out, and_9_out,
       and_10_out, nand_1_out, nor_2_out, nor_3_out, not_1_out, not_2_out, not_3_out, not_4_out, not_5_out,
       not_6_out, or_1_out, or_2_out, or_3_out, or_9_out, xor_1_out;
  wire [2:0] ans01;
  wire [3:0] ans00;
  wire [3:1] ans10, ans11;

  or or_1 (or_1_out, In[1], In[0]);
  and and_1 (and_1_out, In[3], In[0]);
  and and_2 (and_2_out, In[3], In[1]);
  or or_2 (or_2_out, In[1], In[0]);
  and and_3 (and_3_out, In[2], or_1_out);
  not not_1 (not_1_out, In[1]);
  xor xor_1 (xor_1_out, In[2], In[0]);
  or or_3 (or_3_out, In[2], In[1]);
  nor nor_1 (ans00[0], and_2_out, In[0]);
  xnor xnor_1 (ans00[1], In[1], In[0]);
  xor xor_2 (ans00[2], In[2], or_2_out);
  or or_4 (ans00[3], In[3], and_3_out);
  xor xor_3 (ans01[0], In[1], In[0]);
  xor xor_4 (ans01[1], In[2], In[1]);
  or or_5 (ans01[2], In[3], In[2]);
  nor nor_2 (nor_2_out, not_2_out, In[0]);
  not not_2 (not_2_out, In[1]);
  and and_4 (and_4_out, In[2], not_3_out, In[0]);
  not not_3 (not_3_out, In[1]);
  and and_5 (and_5_out, In[2], In[1]);
  and and_6 (and_6_out, not_1_out, xor_1_out);
  and and_7 (and_7_out, In[0], or_3_out);
  or or_6 (ans11[2], and_5_out, and_1_out, and_6_out);
  or or_7 (ans11[3], In[3], and_7_out);
  or or_8 (ans11[1], In[3], nor_2_out, and_4_out);
  Multiplexer #(.Bits(4), .Selector_Bits(2)) multiplexer_1 (
    .sel(Selector), .in_0(ans00), .in_1({In[3], ans01}), .in_2({ans10, In[0]}), .in_3({ans11, In[0]}),
    .out(Output));
  not not_4 (not_4_out, In[1]);
  not not_5 (not_5_out, In[1]);
  not not_6 (not_6_out, In[1]);
  nand nand_1 (nand_1_out, not_4_out, In[0]);
  or or_9 (or_9_out, In[1], In[0]);
  nor nor_3 (nor_3_out, In[2], not_5_out);
  and and_8 (and_8_out, In[2], not_6_out, In[0]);
  and and_9 (and_9_out, In[2], nand_1_out);
  and and_10 (and_10_out, In[2], or_9_out);
  or or_10 (ans10[1], In[3], nor_3_out, and_8_out);
  or or_11 (ans10[2], In[3], and_9_out);
  or or_12 (ans10[3], In[3], and_10_out);

  // Other names for the same wires on the sheet: ans10[0] = In[0]; ans11[0] = In[0]; D = In[0]; C = In[1]; B = In[2];
  //   A = In[3]; ans01[3] = In[3]
endmodule
