// Digital circuit digital_03_04.dig as structural Verilog
module digital_03_04 (
  input  [6:0] In,
  output [6:0] Output
);

  wire c1, c2, c3;
  wire [0:0] _7;
  wire [1:1] _6;
  wire [2:2] _5;
  wire [3:3] _4;
  wire [4:4] _3;
  wire [5:5] _2;
  wire [6:6] _1;

  xor xor_1 (c1, In[3], In[2], In[1], In[0]);
  xor xor_2 (c2, In[5], In[4], In[1], In[0]);
  xor xor_3 (c3, In[6], In[4], In[2], In[0]);
  not not_1 (_7[0], In[0]);
  not not_2 (_6[1], In[1]);
  not not_3 (_5[2], In[2]);
  not not_4 (_4[3], In[3]);
  not not_5 (_3[4], In[4]);
  not not_6 (_2[5], In[5]);
  not not_7 (_1[6], In[6]);
  Multiplexer #(.Bits(7), .Selector_Bits(3)) multiplexer_1 (
    .sel({c1, c2, c3}), .in_0(In), .in_1({_1[6], In[5:0]}), .in_2({In[6], _2[5], In[4:0]}),
    .in_3({In[6:5], _3[4], In[3:0]}), .in_4({In[6:4], _4[3], In[2:0]}), .in_5({In[6:3], _5[2], In[1:0]}),
    .in_6({In[6:2], _6[1], In[0]}), .in_7({In[6:1], _7[0]}), .out(Output));

  // Other names for the same wires on the sheet: _0[6:0] = In; _1[5:0] = In[5:0]; _2 (some bits) = {In[6], In[4:0]};
  //   _3 (some bits) = {In[6:5], In[3:0]}; _4 (some bits) = {In[6:4], In[2:0]}; _5 (some bits) = {In[6:3], In[1:0]};
  //   _6 (some bits) = {In[6:2], In[0]}; _7[6:1] = In[6:1]
endmodule
